// Logisim project processor.circ as structural Verilog: 8 circuits, main circuit main
module main (
  input  [31:0] pc,
  input  [31:0] inst,
  output [17:0] immediate,
  output [31:0] immx,
  output [31:0] branchTarget,
  output [31:0] op2,
  output [31:0] op1,
  output [12:0] out_8,
  output [31:0] out_9
);

  wire ALU_flagse, ALU_flagsgt, and_1_out, and_2_out, and_3_out, CLK, clk1, clock_1_out, cq0, cq1, cq2,
       isBeq, isBgt, isCall, isImmediate, isLd, isRet, isSt, isUbranch, isWb, not_1_out, not_2_out,
       not_3_out, not_4_out, or_1_out, undriven;
  wire [4:0] register_1_q;
  wire [31:0] adder_1_out, aluResult, bit_extender_1_out, ldResult, multiplexer_2_out, PC_t, shifter_1_out;

  Register #(.width(5)) register_1 (.D(inst[31:27]), .Q(register_1_q), .clk(clk1));  // open: en, clr
  Clock clock_1 (.out(clock_1_out));
  not not_1 (not_1_out, cq2);
  not not_2 (not_2_out, cq1);
  or or_1 (or_1_out, cq0, not_1_out);
  IF if_1 (.isBranchTaken(undriven), .Instr(inst), .clock(CLK), .PC(PC_t), .Branch_Target(branchTarget));
  controlUnit controlunit_1 (
    .I_bit(inst[26]), .opcode(register_1_q), .isSt(isSt), .isLd(isLd), .isBeq(isBeq), .isBgt(isBgt),
    .isRet(isRet), .isImmediate(isImmediate), .isWb(isWb), .isUbranch(isUbranch), .isCall(isCall),
    .ALUsignals(out_8));
  and and_1 (and_1_out, or_1_out, not_2_out);
  D_Flip_Flop d_ff_1 (.clk(clock_1_out), .D(and_1_out), .Q(cq2));  // open: Qn, preset, en, reset
  not not_3 (not_3_out, cq0);
  and and_2 (and_2_out, not_3_out, cq2);
  D_Flip_Flop d_ff_2 (.clk(clock_1_out), .D(and_2_out), .Q(cq1));  // open: Qn, preset, en, reset
  not not_4 (not_4_out, cq0);
  and and_3 (and_3_out, not_4_out, cq1);
  D_Flip_Flop d_ff_3 (.clk(clock_1_out), .D(and_3_out), .Q(cq0));  // open: Qn, preset, en, reset
  assign bit_extender_1_out = {{5{inst[26]}}, inst[26:0]};  // Bit_Extender bit_extender_1
  calcImmediate calcImmx (.input_18_bit(inst[17:0]), .output_32_bit(immx));
  Shifter #(.width(32)) shifter_1 (.in(bit_extender_1_out), .\dist (5'b00010), .out(shifter_1_out));
  Adder #(.width(32)) adder_1 (.a(shifter_1_out), .b(pc), .out(adder_1_out), .cin(1'b0));  // open: cout
  registerFile registerfile_1 (
    .Clock(CLK), .rs2(inst[17:14]), .rs1(inst[21:18]), .rd(inst[25:22]), .aluResult(aluResult),
    .ldResult(ldResult), .pc(PC_t), .isLd(isLd), .isCall(isCall), .isSt(isSt), .isRet(isRet), .Op2(op2),
    .Op1(op1));
  Multiplexer #(.width(32), .enable("false")) multiplexer_1 (
    .in0(adder_1_out), .in1(op1), .out(branchTarget), .sel(isRet));
  Multiplexer #(.width(32), .enable("false")) multiplexer_2 (
    .in0(op2), .in1(immx), .out(multiplexer_2_out), .sel(isImmediate));
  ALU ALU (
    .A(op1), .B(multiplexer_2_out), .aluResult(aluResult), .ALUsignals(out_8), .FlagsGT(ALU_flagsgt),
    .FlagsE(ALU_flagse));
  EF Branch_Unit (
    .isUbranch(isUbranch), .isBeq(isBeq), .FlagsE(ALU_flagse), .FlagsGT(ALU_flagsgt), .isBGt(isBgt),
    .isBranchTaken(undriven));
  MA ma_1 (.aluResult(aluResult), .op2(op2), .isSt(isSt), .Clock(CLK), .isLd(isLd), .ldResult(ldResult));

  assign immediate = inst[17:0];
  assign out_9 = inst;

  // Other names for the same wires on the sheet: I_bit = inst[26]; ALUsignals[12:0] = out_8;
  //   opcode[4:0] = inst[31:27]; rd[3:0] = inst[25:22]; rs1[3:0] = inst[21:18]; rs2[3:0] = inst[17:14]

  // Notes on the sheet:
  //   #######################################
  //   rs2
  //   rs1
  //   rd
  //   Registers
endmodule

module IF (
  input  isBranchTaken,
  input  [31:0] Branch_Target,
  input  clock,
  output [31:0] PC,
  output [31:0] Instr
);

  wire [23:0] bit_extender_1_out;
  wire [31:0] adder_1_out, multiplexer_1_out;

  Register #(.width(32)) u_PC (.D(multiplexer_1_out), .en(1'b1), .Q(PC), .clk(clock), .clr(1'b0));
  Multiplexer #(.width(32), .enable("false")) multiplexer_1 (
    .in0(adder_1_out), .in1(Branch_Target), .out(multiplexer_1_out), .sel(isBranchTaken));
  Adder #(.width(32)) adder_1 (.a(32'h1), .b(PC), .out(adder_1_out), .cin(1'b0));  // open: cout
  Bit_Extender #(.in_width(32), .out_width(24)) bit_extender_1 (.in(PC), .out(bit_extender_1_out));
  RAM #(.addrWidth(24), .dataWidth(32), .bus("separate")) ram_1 (
    .addr(bit_extender_1_out), .data(Instr), .str(1'b0), .sel(1'b1), .clk(clock), .ld(1'b1));  // open: din, clr
  // also tied to GND on the sheet: isBranchTaken

  // Other names for the same wires on the sheet: BranchTarget[31:0] = Branch_Target
endmodule

module registerFile (
  input  Clock,
  input  [3:0] rs2,
  input  [3:0] rs1,
  input  [3:0] rd,
  input  isSt,
  input  isRet,
  input  [31:0] aluResult,
  input  [31:0] ldResult,
  input  [31:0] pc,
  input  isLd,
  input  isCall,
  output [31:0] Op2,
  output [31:0] Op1
);

  wire [3:0] multiplexer_2_out, multiplexer_3_out, multiplexer_6_out;
  wire [31:0] adder_1_out, multiplexer_1_out, r0, r1, r2, r3, r4, r5, r6, r7, r8, r9, r10, r11, r12, r13,
       r14, r15, wr0, wr1, wr2, wr3, wr4, wr5, wr6, wr7, wr8, wr9, wr10, wr11, wr12, wr13, wr14, wr15;

  Register #(.width(32)) u_r0 (.D(wr0), .en(1'b1), .Q(r0), .clk(Clock));  // open: clr
  Register #(.width(32)) u_r4 (.D(wr4), .en(1'b1), .Q(r4), .clk(Clock));  // open: clr
  Register #(.width(32)) u_r8 (.D(wr8), .en(1'b1), .Q(r8), .clk(Clock));  // open: clr
  Register #(.width(32)) u_r12 (.D(wr12), .en(1'b1), .Q(r12), .clk(Clock));  // open: clr
  Adder #(.width(32)) adder_1 (.a(pc), .b(32'h1), .out(adder_1_out), .cin(1'b0));  // open: cout
  Register #(.width(32)) u_r1 (.D(wr1), .en(1'b1), .Q(r1), .clk(Clock));  // open: clr
  Register #(.width(32)) u_r5 (.D(wr5), .en(1'b1), .Q(r5), .clk(Clock));  // open: clr
  Register #(.width(32)) u_r9 (.D(wr9), .en(1'b1), .Q(r9), .clk(Clock));  // open: clr
  Register #(.width(32)) u_r13 (.D(wr13), .en(1'b1), .Q(r13), .clk(Clock));  // open: clr
  Multiplexer #(.select(2), .width(32), .enable("false")) multiplexer_1 (
    .in0(aluResult), .in1(ldResult), .in2(adder_1_out), .out(multiplexer_1_out), .sel({isCall, isLd}));  // open: in3
  Register #(.width(32)) u_r2 (.D(wr2), .en(1'b1), .Q(r2), .clk(Clock));  // open: clr
  Register #(.width(32)) u_r6 (.D(wr6), .en(1'b1), .Q(r6), .clk(Clock));  // open: clr
  Register #(.width(32)) u_r10 (.D(wr10), .en(1'b1), .Q(r10), .clk(Clock));  // open: clr
  Register #(.width(32)) u_r14 (.D(wr14), .en(1'b1), .Q(r14), .clk(Clock));  // open: clr
  Multiplexer #(.width(4), .enable("false")) multiplexer_2 (
    .in0(rd), .in1(4'b1111), .out(multiplexer_2_out), .sel(isCall));
  Demultiplexer #(.select(4), .width(32), .enable("false")) demultiplexer_1 (
    .out0(wr0), .out1(wr1), .out2(wr2), .out3(wr3), .out4(wr4), .out5(wr5), .out6(wr6), .out7(wr7),
    .out8(wr8), .out9(wr9), .out10(wr10), .out11(wr11), .out12(wr12), .out13(wr13), .out14(wr14),
    .out15(wr15), .in(multiplexer_1_out), .sel(multiplexer_2_out));
  Register #(.width(32)) u_r3 (.D(wr3), .en(1'b1), .Q(r3), .clk(Clock));  // open: clr
  Register #(.width(32)) u_r7 (.D(wr7), .en(1'b1), .Q(r7), .clk(Clock));  // open: clr
  Register #(.width(32)) u_r11 (.D(wr11), .en(1'b1), .Q(r11), .clk(Clock));  // open: clr
  Register #(.width(32)) u_r15 (.D(wr15), .en(1'b1), .Q(r15), .clk(Clock));  // open: clr
  Multiplexer #(.width(4), .enable("false")) multiplexer_3 (.in0(rs2), .in1(rd), .out(multiplexer_3_out), .sel(isSt));
  Multiplexer #(.select(4), .width(32), .enable("false")) multiplexer_4 (
    .in0(r0), .in1(r1), .in2(r2), .in3(r3), .in4(r4), .in5(r5), .in6(r6), .in7(r7), .in8(r8), .in9(r9),
    .in10(r10), .in11(r11), .in12(r12), .in13(r13), .in14(r14), .in15(r15), .out(Op2), .sel(multiplexer_3_out));
  Multiplexer #(.select(4), .width(32), .enable("false")) multiplexer_5 (
    .in0(r0), .in1(r1), .in2(r2), .in3(r3), .in4(r4), .in5(r5), .in6(r6), .in7(r7), .in8(r8), .in9(r9),
    .in10(r10), .in11(r11), .in12(r12), .in13(r13), .in14(r14), .in15(r15), .out(Op1), .sel(multiplexer_6_out));
  Multiplexer #(.width(4), .enable("false")) multiplexer_6 (
    .in0(rs1), .in1(4'b1111), .out(multiplexer_6_out), .sel(isRet));

  // Other names for the same wires on the sheet: clk = Clock

  // Notes on the sheet:
  //   ra
  //   ra
endmodule

module calcImmediate (
  input  [17:0] input_18_bit,
  output [31:0] output_32_bit
);

  wire [15:0] bit_extender_1_out;
  wire [31:0] bit_extender_2_out, bit_extender_3_out, bit_extender_4_out, shifter_1_out;

  Bit_Extender #(.in_width(18)) bit_extender_1 (.in(input_18_bit), .out(bit_extender_1_out));
  assign bit_extender_2_out = {{16{bit_extender_1_out[15]}}, bit_extender_1_out};  // Bit_Extender bit_extender_2
  assign bit_extender_3_out = {{16{1'b0}}, bit_extender_1_out};  // Bit_Extender bit_extender_3
  assign bit_extender_4_out = {{16{1'b0}}, bit_extender_1_out};  // Bit_Extender bit_extender_4
  Shifter #(.width(32)) shifter_1 (.in(bit_extender_4_out), .\dist (5'b10000), .out(shifter_1_out));
  Multiplexer #(.select(2), .width(32), .enable("false")) multiplexer_1 (
    .in0(bit_extender_2_out), .in1(bit_extender_3_out), .in2(shifter_1_out), .out(output_32_bit),
    .sel(input_18_bit[17:16]));  // open: in3
endmodule

module ALU (
  input  [12:0] ALUsignals,
  input  [31:0] A,
  input  [31:0] B,
  output FlagsGT,
  output [31:0] aluResult,
  output FlagsE
);

  wire comparator_1_gt, comparator_2_eq, multiplexer_4_out, multiplexer_5_out, not_2_out, not_6_out,
       not_7_out, not_8_out, not_10_out, or_1_out, transmission_10_p1;
  wire [4:0] bit_extender_1_out, bit_extender_2_out, bit_extender_3_out;
  wire [31:0] adder_1_out, and_1_out, divider_1_out, multiplexer_1_out, multiplexer_2_out, multiplexer_3_out,
       multiplier_1_out, not_1_out, or_2_out, shifter_1_out, shifter_2_out, shifter_3_out, subtractor_1_out;

  Multiplexer #(.width(32), .enable("false")) multiplexer_1 (
    .in0(A), .in1(B), .out(multiplexer_1_out), .sel(ALUsignals[5]));
  Multiplexer #(.width(32), .enable("false")) multiplexer_2 (
    .in0(B), .in1(multiplier_1_out), .out(multiplexer_2_out), .sel(ALUsignals[5]));
  Multiplexer #(.width(32), .enable("false")) multiplexer_3 (
    .in0(B), .in1(divider_1_out), .out(multiplexer_3_out), .sel(ALUsignals[5]));
  Adder #(.width(32)) adder_1 (.a(A), .b(B), .out(adder_1_out), .cin(1'b0));  // open: cout
  Subtractor #(.width(32)) subtractor_1 (
    .a(A), .b(multiplexer_2_out), .out(subtractor_1_out), .bin(1'b0));  // open: bout
  Multiplier #(.width(32)) multiplier_1 (
    .a(multiplexer_1_out), .b(multiplexer_3_out), .out(multiplier_1_out), .cin({32{1'b0}}));  // open: cout
  Divider #(.width(32)) divider_1 (.a(A), .b(B), .out(divider_1_out), .upper({32{1'b0}}));  // open: rem
  Shifter #(.width(32)) shifter_1 (.in(A), .\dist (bit_extender_1_out), .out(shifter_1_out));
  Bit_Extender #(.in_width(32), .out_width(5)) bit_extender_1 (.in(B), .out(bit_extender_1_out));
  Bit_Extender #(.in_width(32), .out_width(5)) bit_extender_2 (.in(B), .out(bit_extender_2_out));
  Bit_Extender #(.in_width(32), .out_width(5)) bit_extender_3 (.in(B), .out(bit_extender_3_out));
  or or_1 (or_1_out, ALUsignals[2], ALUsignals[5]);
  Shifter #(.width(32), .shift("lr")) shifter_2 (.in(A), .\dist (bit_extender_2_out), .out(shifter_2_out));
  Shifter #(.width(32), .shift("ar")) shifter_3 (.in(A), .\dist (bit_extender_3_out), .out(shifter_3_out));
  assign and_1_out = A & B;  // AND_Gate and_1, 32 bits wide
  assign or_2_out = A | B;  // OR_Gate or_2, 32 bits wide
  assign not_1_out = ~A;  // NOT_Gate not_1, 32 bits wide
  not not_2 (not_2_out, or_1_out);
  // Transmission_Gate #(.width(32)) transmission_1: pin names not known; wires that end beside it: subtractor_1_out, not_2_out, or_1_out, aluResult
  // NOT_Gate not_3 has open pins: in=ALUsignals[4], out=open
  // Transmission_Gate #(.width(32)) transmission_2: pin names not known; wires that end beside it: divider_1_out, ALUsignals[4], aluResult
  // NOT_Gate not_4 has open pins: in=ALUsignals[7], out=open
  // Transmission_Gate #(.width(32)) transmission_3: pin names not known; wires that end beside it: shifter_1_out, ALUsignals[7], aluResult
  // NOT_Gate not_5 has open pins: in=ALUsignals[8], out=open
  // Transmission_Gate #(.width(32)) transmission_4: pin names not known; wires that end beside it: shifter_2_out, ALUsignals[8], aluResult
  not not_6 (not_6_out, ALUsignals[9]);
  // Transmission_Gate #(.width(32)) transmission_5: pin names not known; wires that end beside it: shifter_3_out, not_6_out, ALUsignals[9], aluResult
  not not_7 (not_7_out, ALUsignals[11]);
  not not_8 (not_8_out, ALUsignals[12]);
  // NOT_Gate not_9 has open pins: in=ALUsignals[3], out=open
  // Transmission_Gate #(.width(32)) transmission_6: pin names not known; wires that end beside it: multiplier_1_out, ALUsignals[3], aluResult
  // Transmission_Gate #(.width(32)) transmission_7: pin names not known; wires that end beside it: and_1_out, not_7_out, ALUsignals[11], aluResult
  // Transmission_Gate #(.width(32)) transmission_8: pin names not known; wires that end beside it: or_2_out, not_8_out, ALUsignals[12], aluResult
  not not_10 (not_10_out, ALUsignals[10]);
  // Transmission_Gate #(.width(32)) transmission_9: pin names not known; wires that end beside it: not_1_out, not_10_out, ALUsignals[10], aluResult
  // Transmission_Gate #(.width(32)) transmission_10: pin names not known; wires that end beside it: transmission_10_p1, adder_1_out, aluResult, ALUsignals[1]
  not not_11 (transmission_10_p1, ALUsignals[1]);
  Comparator #(.width(32)) comparator_1 (.a(A), .b(B), .gt(comparator_1_gt));  // open: eq, lt
  Comparator #(.width(32)) comparator_2 (.a(A), .b(B), .eq(comparator_2_eq));  // open: gt, lt
  Multiplexer #(.enable("false")) multiplexer_4 (
    .in0(FlagsGT), .in1(comparator_1_gt), .out(multiplexer_4_out), .sel(ALUsignals[0]));
  Multiplexer #(.enable("false")) multiplexer_5 (
    .in0(FlagsE), .in1(comparator_2_eq), .out(multiplexer_5_out), .sel(ALUsignals[0]));
  D_Flip_Flop d_ff_1 (.D(multiplexer_4_out), .Q(FlagsGT));  // open: clk, Qn, preset, en, reset
  D_Flip_Flop d_ff_2 (.D(multiplexer_5_out), .Q(FlagsE));  // open: clk, Qn, preset, en, reset

  // Other names for the same wires on the sheet: isCmp = ALUsignals[0]; isAdd = ALUsignals[1]; isSub = ALUsignals[2];
  //   isMul = ALUsignals[3]; isDiv = ALUsignals[4]; isMod = ALUsignals[5]; isMov = ALUsignals[6];
  //   isLsl = ALUsignals[7]; isLsr = ALUsignals[8]; isAsr = ALUsignals[9]; isNot = ALUsignals[10];
  //   isAnd = ALUsignals[11]; isOr = ALUsignals[12]
endmodule

module EF (
  input  isUbranch,
  input  isBeq,
  input  isBranchTaken,
  input  FlagsE,
  input  FlagsGT,
  input  isBGt
);

  wire and_1_out, and_2_out;

  and and_1 (and_1_out, isBeq, FlagsE);
  and and_2 (and_2_out, FlagsGT, isBGt);
  or or_1 (isBranchTaken, isUbranch, and_1_out, and_2_out);
endmodule

module MA (
  input  [31:0] aluResult,
  input  [31:0] op2,
  input  isSt,
  input  isLd,
  input  Clock,
  output [31:0] ldResult
);

  wire [23:0] bit_extender_1_out;
  wire [31:0] shifter_1_out;

  Bit_Extender #(.in_width(32), .out_width(24)) bit_extender_1 (.in(shifter_1_out), .out(bit_extender_1_out));
  Shifter #(.width(32), .shift("lr")) shifter_1 (.in(aluResult), .\dist (5'b00010), .out(shifter_1_out));
  RAM #(.addrWidth(24), .dataWidth(32), .bus("separate")) ram_1 (
    .addr(bit_extender_1_out), .din(op2), .data(ldResult), .str(isSt), .sel(1'b1), .clk(Clock), .ld(isLd),
    .clr(1'b0));
endmodule

module controlUnit (
  input  I_bit,
  input  [4:0] opcode,
  output isSt,
  output isLd,
  output isBeq,
  output isBgt,
  output isRet,
  output isImmediate,
  output isWb,
  output isUbranch,
  output isCall,
  output [12:0] ALUsignals
);

  wire and_6_out, and_7_out, and_8_out, and_9_out, and_10_out, and_12_out, and_13_out, nand_1_out;

  nand nand_1 (nand_1_out, opcode[0], opcode[1]);
  and and_1 (isSt, opcode[0], opcode[1], opcode[2], opcode[3], ~opcode[4]);  // AND_Gate
  and and_2 (isLd, ~opcode[0], opcode[1], opcode[2], opcode[3], ~opcode[4]);  // AND_Gate
  and and_3 (isBeq, ~opcode[0], ~opcode[1], ~opcode[2], ~opcode[3], opcode[4]);  // AND_Gate
  and and_4 (isBgt, opcode[0], ~opcode[1], ~opcode[2], ~opcode[3], opcode[4]);  // AND_Gate
  and and_5 (isRet, ~opcode[0], ~opcode[1], opcode[2], ~opcode[3], opcode[4]);  // AND_Gate
  and and_6 (and_6_out, opcode[0], ~opcode[1], opcode[2], ~opcode[4]);  // AND_Gate
  and and_7 (and_7_out, opcode[0], opcode[2], opcode[3], ~opcode[4]);  // AND_Gate
  and and_8 (and_8_out, opcode[4], nand_1_out);
  and and_9 (and_9_out, opcode[1], ~opcode[2], ~opcode[3], opcode[4]);  // AND_Gate
  and and_10 (and_10_out, ~opcode[0], ~opcode[1], opcode[2], ~opcode[3], opcode[4]);  // AND_Gate
  and and_11 (isCall, opcode[0], opcode[1], ~opcode[2], ~opcode[3], opcode[4]);  // AND_Gate
  and and_12 (and_12_out, ~opcode[0], ~opcode[1], ~opcode[2], ~opcode[3], ~opcode[4]);  // AND_Gate
  and and_13 (and_13_out, opcode[1], opcode[2], opcode[3], ~opcode[4]);  // AND_Gate
  and isSub (ALUsignals[2], opcode[0], ~opcode[1], ~opcode[2], ~opcode[3], ~opcode[4]);  // AND_Gate
  and isCmp (ALUsignals[0], opcode[0], ~opcode[1], opcode[2], ~opcode[3], ~opcode[4]);  // AND_Gate
  and isMul (ALUsignals[3], ~opcode[0], opcode[1], ~opcode[2], ~opcode[3], ~opcode[4]);  // AND_Gate
  and isDiv (ALUsignals[4], opcode[0], opcode[1], ~opcode[2], ~opcode[3], ~opcode[4]);  // AND_Gate
  and isMod (ALUsignals[5], ~opcode[0], ~opcode[1], opcode[2], ~opcode[3], ~opcode[4]);  // AND_Gate
  and isLsl (ALUsignals[7], ~opcode[0], opcode[1], ~opcode[2], opcode[3], ~opcode[4]);  // AND_Gate
  and isLsr (ALUsignals[8], opcode[0], opcode[1], ~opcode[2], opcode[3], ~opcode[4]);  // AND_Gate
  and isAsr (ALUsignals[9], ~opcode[0], ~opcode[1], opcode[2], opcode[3], ~opcode[4]);  // AND_Gate
  and isOr (ALUsignals[12], opcode[0], opcode[1], opcode[2], ~opcode[3], ~opcode[4]);  // AND_Gate
  and isAnd (ALUsignals[11], ~opcode[0], opcode[1], opcode[2], ~opcode[3], ~opcode[4]);  // AND_Gate
  and isNot (ALUsignals[10], ~opcode[0], ~opcode[1], ~opcode[2], opcode[3], ~opcode[4]);  // AND_Gate
  and isMov (ALUsignals[6], opcode[0], ~opcode[1], ~opcode[2], opcode[3], ~opcode[4]);  // AND_Gate
  nor nor_1 (isWb, and_6_out, and_7_out, and_8_out);
  or or_1 (isUbranch, and_9_out, and_10_out);
  or isAdd (ALUsignals[1], and_12_out, and_13_out);

  assign isImmediate = I_bit;

  // Notes on the sheet:
  //   op1
  //   op2
  //   op3
  //   op4
  //   op5
endmodule
